# Fritzing sketch schematic_automatic_irrigation_system (saved by Fritzing 0.9.3b)
breadboards: 1

parts:
  Componente1 = Arduino Uno (Rev3) - ICSP
  M1 = DC Motor
  Componente2 = FC-28 Soil Hygrometer Module
  Componente3 = FC-28 Soil Hygrometer Module - Probe
  LED1 = smd LED [color="Red (633nm)" package="0603 [SMD]"]
  R2 = Resistor [tolerance=±5% resistance=1k package=THT]
  LED2 = smd LED [color="Green (555nm)" package="0603 [SMD]"]
  R3 = Resistor [tolerance=±5% resistance=1k package=THT]
  T122 = npn-Powertransistor [package="TO220 [THT]"]
  BAT1 = BC9VPC [package=bc9vpc]

nets:
  N1: Componente1.A0, Componente2.AO
  GND: Componente1.GND, M1.pin_1, Componente2.GND, R2.Pin_1, R3.Pin_1, T122.base, BAT1.V-
  N2: Componente1.D4, LED1.anode
  N3: Componente1.D5_PWM, LED2.anode
  N4: Componente1.D6_PWM, T122.emitter
  5V: Componente1.5V, Componente2.VCC, BAT1.V+
  N5: M1.pin_2, T122.collector
  N6: Componente2.POS, Componente3.POS
  N7: Componente2.NEG, Componente3.NEG
  N8: LED1.cathode, R2.Pin_0
  N9: LED2.cathode, R3.Pin_0

notes:
  Sensor do nível de umidade do solo.
  Esse motor simboliza a bomba d'água

custom parts:
  FC-28 Soil Hygrometer Module: The FC-28 is a soil hygrometer module that uses the Texas Instruments LM393 comparator chip to provide an analog measurement of soil humidity. The digital output is high when soil moisture is over a certain threshold, as determined by adjusting the potentiometer.
  FC-28 Soil Hygrometer Module - Probe: The FC-28 is a soil hygrometer module that uses the Texas Instruments LM393 comparator chip to provide an analog measurement of soil humidity.
